# Fritzing sketch cab-floor-power-2 (saved by Fritzing 0.9.4)
breadboards: 1

parts:
  BS170 = PNP-Transistor [package="TO92 [THT]"]
  1k1 = Resistor [tolerance=±5% resistance=220 package=THT]
  D4 = Rectifier Diode [part_number=1N4001 package="300 mil [THT]"]
  D5 = Rectifier Diode [part_number=1N4001 package="300 mil [THT]"]
  100k1 = Resistor [tolerance=±5% resistance=220 package=THT]
  100k2 = Resistor [tolerance=±5% resistance=220 package=THT]
  MOC3064 = Optocoupler [package=THT]
  SRD-03VDC-SL-C1 = srd-05vdc-sl-c
  510 = Resistor [tolerance=±5% resistance=220 package=THT]
  Power_3_4 = Battery
  D6 = Rectifier Diode [part_number=1N4001 package="300 mil [THT]"]
  1k2 = Resistor [tolerance=±5% resistance=220 package=THT]
  Input_signal1 = Screw terminal - 2 pins [package=THT]
  LED_Relay1 = Screw terminal - 2 pins [package=THT]
  1mF = Electrolytic Capacitor [capacitance=1µF package="100 mil [THT, electrolytic]"]
  1mF2 = Electrolytic Capacitor [capacitance=1µF package="100 mil [THT, electrolytic]"]
  BTA12-601 = Basic FET P-Channel [package="TO220 [THT]"]
  360 = Resistor [tolerance=±5% resistance=220 package=THT]
  360_2 = Resistor [tolerance=±5% resistance=220 package=THT]
  BS170_2 = PNP-Transistor [package="TO92 [THT]"]

nets:
  N1: BS170.E, Power_3_4.-, Input_signal1.pin1, 1mF.-, 1mF2.-, BS170_2.E
  N2: BS170.B, D5.cathode, 100k1.Pin_0, 1mF2.+
  N3: BS170.C, MOC3064.Pin_2
  N4: 1k1.Pin_0, D4.cathode, D5.anode, 100k1.Pin_1, 100k2.Pin_1
  N5: 1k1.Pin_1, Input_signal1.pin2
  N6: D4.anode, 100k2.Pin_0
  N7: MOC3064.Pin_1, 510.Pin_1
  N8: MOC3064.Pin_4, BTA12-601.source, 360_2.Pin_1
  N9: MOC3064.Pin_6, 360.Pin_1
  N10: SRD-03VDC-SL-C1.pin_1, D6.anode, LED_Relay1.pin1, BS170_2.C
  N11: SRD-03VDC-SL-C1.pin_2, BTA12-601.gate, 360.Pin_0
  N12: SRD-03VDC-SL-C1.pin_4, 510.Pin_0, Power_3_4.+, D6.cathode, 1k2.Pin_1
  N13: SRD-03VDC-SL-C1.pin_5, BTA12-601.drain, 360_2.Pin_0
  N14: 1k2.Pin_0, LED_Relay1.pin2
  N15: 1mF.+, BS170_2.B
