# Fritzing sketch cab-floor-power (saved by Fritzing 0.9.4)
breadboards: 1

parts:
  BS170 = PNP-Transistor [package="TO92 [THT]"]
  1k = Resistor [tolerance=±5% resistance=220 package=THT]
  D1 = Rectifier Diode [part_number=1N4001 package="300 mil [THT]"]
  D2 = Rectifier Diode [part_number=1N4001 package="300 mil [THT]"]
  100k = Resistor [tolerance=±5% resistance=220 package=THT]
  100k_2 = Resistor [tolerance=±5% resistance=220 package=THT]
  BS170_2 = PNP-Transistor [package="TO92 [THT]"]
  MOC3063 = Optocoupler [package=THT]
  SRD-03VDC-SL-C = srd-05vdc-sl-c
  510 = Resistor [tolerance=±5% resistance=220 package=THT]
  Power_3_3 = Battery
  D3 = Rectifier Diode [part_number=1N4001 package="300 mil [THT]"]
  1k_2 = Resistor [tolerance=±5% resistance=220 package=THT]
  LED_Relay = Screw terminal - 2 pins [package=THT]
  1mF = Electrolytic Capacitor [capacitance=1µF package="100 mil [THT, electrolytic]"]
  1mF_2 = Electrolytic Capacitor [capacitance=1µF package="100 mil [THT, electrolytic]"]
  BTA12-600 = Basic FET P-Channel [package="TO220 [THT]"]
  360 = Resistor [tolerance=±5% resistance=220 package=THT]
  360_2 = Resistor [tolerance=±5% resistance=220 package=THT]
  Input_signal = Screw terminal - 2 pins [package=THT]

nets:
  N1: BS170.E, MOC3063.Pin_2
  N2: BS170.B, D2.cathode, 100k.Pin_0, 1mF_2.+
  N3: BS170.C, BS170_2.C, Power_3_3.-, 1mF.-, 1mF_2.-, Input_signal.pin1
  N4: 1k.Pin_0, D1.cathode, D2.anode, 100k.Pin_1, 100k_2.Pin_1
  N5: 1k.Pin_1, Input_signal.pin2
  N6: D1.anode, 100k_2.Pin_0, BS170_2.B, 1mF.+
  N7: BS170_2.E, SRD-03VDC-SL-C.pin_1, D3.anode, LED_Relay.pin1
  N8: MOC3063.Pin_1, 510.Pin_1
  N9: MOC3063.Pin_4, BTA12-600.source, 360_2.Pin_1
  N10: MOC3063.Pin_6, 360.Pin_1
  N11: SRD-03VDC-SL-C.pin_2, BTA12-600.drain, 360_2.Pin_0
  N12: SRD-03VDC-SL-C.pin_3, BTA12-600.gate, 360.Pin_0
  N13: SRD-03VDC-SL-C.pin_4, 510.Pin_0, Power_3_3.+, D3.cathode, 1k_2.Pin_1
  N14: 1k_2.Pin_0, LED_Relay.pin2
