# Fritzing sketch cab-floor (saved by Fritzing 0.9.4)
breadboards: 1

parts:
  A1 = Wemos S2 Mini [part_number="WeMos D1 Mini Lite"]
  ADDR_28_60_61_81_E3_BE_3C_B7 = DS18B20 1-Wire Temperature Sensor [part_number=DS18B20]
  OLED1 = OLED Mono 0.56 inch blue or white
  DHT1 = DHT11 Humitidy and Temperature Sensor

nets:
  N1: A1.Pin_1, A1.Pin_9
  N2: A1.Pin_2, A1.Pin_10, DHT1.DATA
  N3: A1.Pin_3, A1.Pin_11, ADDR_28_60_61_81_E3_BE_3C_B7.DQ
  N4: A1.Pin_4, A1.Pin_12
  N5: A1.Pin_5, A1.Pin_13
  N6: A1.Pin_6, A1.Pin_14, OLED1.SCL
  N7: A1.Pin_7, A1.Pin_15, OLED1.SDA
  N8: A1.Pin_8, A1.Pin_16, ADDR_28_60_61_81_E3_BE_3C_B7.VDD
  VCC: A1.Pin_17, A1.Pin_25, OLED1.VCC, DHT1.VDD
  GND: A1.Pin_18, A1.Pin_26, ADDR_28_60_61_81_E3_BE_3C_B7.GND, OLED1.GND, DHT1.GND
  N9: A1.Pin_19, A1.Pin_27
  N10: A1.Pin_20, A1.Pin_28
  N11: A1.Pin_21, A1.Pin_29
  N12: A1.Pin_22, A1.Pin_30
  N13: A1.Pin_23, A1.Pin_31
  N14: A1.Pin_24, A1.Pin_32

custom parts:
  Wemos S2 Mini: A mini wifi board based on the ESP32-S2FN4R2.
  OLED Mono 0.56 inch blue or white: OLED, I2C 3.3V - 5V Blue and White text versions
  DHT11 Humitidy and Temperature Sensor: DHT11 Humidity and Temperature Sensor
